// Logisim project computer.circ as structural Verilog: 11 circuits, main circuit main
module main (
  input  reset,
  output [7:0] out_2,
  output [27:0] out_3,
  output [7:0] out_4
);

  wire frequencydiviser_1_clock_dirac, frequencydiviser_1_clock_instruction,
       instructiondecoder_1_fu_enable_output, instructiondecoder_1_fu_output_alu_or_shifter,
       instructiondecoder_1_ram_enable_read, instructiondecoder_1_ram_enable_write,
       instructiondecoder_1_rf_enable_write, pc_clock_out;
  wire [1:0] instructiondecoder_1_fu_select_shifter, instructiondecoder_1_rf_address_output_a,
       instructiondecoder_1_rf_address_output_b, instructiondecoder_1_rf_address_write;
  wire [3:0] instructiondecoder_1_fu_select_alu;
  wire [7:0] Data_Memory_dout, instructiondecoder_1_ram_address, registerfile_1_output_a,
       registerfile_1_output_b;

  Clock pc_clock (.out(pc_clock_out));
  ProgramCounter programcounter_1 (
    .reset(reset), .increment(frequencydiviser_1_clock_instruction), .Instruction_pointer(out_4));
  ROM #(.dataWidth(28)) Instruction_Memory (.addr(out_4), .data(out_3));
  frequencyDiviser frequencydiviser_1 (
    .clock(pc_clock_out), .clock_instruction(frequencydiviser_1_clock_instruction),
    .clock_dirac(frequencydiviser_1_clock_dirac));  // open: out_4
  LED led_1 (.in(frequencydiviser_1_clock_instruction));
  InstructionDecoder instructiondecoder_1 (
    .Instruction(out_3[27:24]), .variable_A(out_3[23:16]), .variable_B(out_3[15:8]), .variable_C(out_3[7:0]),
    .RF_enable_write(instructiondecoder_1_rf_enable_write),
    .RF_address_write(instructiondecoder_1_rf_address_write),
    .RF_address_output_A(instructiondecoder_1_rf_address_output_a),
    .RF_address_output_B(instructiondecoder_1_rf_address_output_b),
    .FU_select_alu(instructiondecoder_1_fu_select_alu),
    .FU_select_shifter(instructiondecoder_1_fu_select_shifter),
    .FU_enable_output(instructiondecoder_1_fu_enable_output),
    .FU_output_alu_or_shifter(instructiondecoder_1_fu_output_alu_or_shifter),
    .RAM_enable_write(instructiondecoder_1_ram_enable_write),
    .RAM_enable_read(instructiondecoder_1_ram_enable_read), .RAM_address(instructiondecoder_1_ram_address));  // open: next_instruction, PC_next_instruction
  RegisterFile registerfile_1 (
    .Input_RF(out_2), .enable_write(instructiondecoder_1_rf_enable_write),
    .address_write(instructiondecoder_1_rf_address_write),
    .address_output_A(instructiondecoder_1_rf_address_output_a),
    .address_output_B(instructiondecoder_1_rf_address_output_b), .clock(frequencydiviser_1_clock_dirac),
    .Output_A(registerfile_1_output_a), .Output_B(registerfile_1_output_b));
  FunctionUnit functionunit_1 (
    .Input_A(registerfile_1_output_a), .Input_B(registerfile_1_output_b),
    .select_alu(instructiondecoder_1_fu_select_alu), .select_shifter(instructiondecoder_1_fu_select_shifter),
    .select_alu_or_shifter(instructiondecoder_1_fu_output_alu_or_shifter),
    .enable_ouput(instructiondecoder_1_fu_enable_output), .Output_FU(out_2));  // open: overflow
  assign out_2 = instructiondecoder_1_ram_enable_read ? Data_Memory_dout : 8'bz;  // Controlled_Buffer controlled_buffer_1
  RAM Data_Memory (
    .addr(instructiondecoder_1_ram_address), .we(instructiondecoder_1_ram_enable_write),
    .oe(instructiondecoder_1_ram_enable_read), .clk(frequencydiviser_1_clock_dirac),
    .din(registerfile_1_output_a), .dout(Data_Memory_dout));

  // Notes on the sheet:
  //   contents of Instruction_Memory (hex, n*v repeats v):
  //   4000000 4010100 2020001 3020300
endmodule

module ram_perso (
  input  [7:0] address,
  input  write_enable,
  input  [7:0] input_word,
  input  in_4,
  output [7:0] output_word
);

  wire clock_1_out, not_1_out;
  wire [7:0] address_register_q, input_register_q, ram_1_dout;

  Clock clock_1 (.out(clock_1_out));
  Register address_register (.D(address), .en(in_4), .clk(clock_1_out), .Q(address_register_q));  // open: clr
  Register input_register (.D(input_word), .en(in_4), .clk(clock_1_out), .Q(input_register_q));  // open: clr
  Register output_register (.D(ram_1_dout), .en(in_4), .clk(clock_1_out), .Q(output_word));  // open: clr
  not not_1 (not_1_out, write_enable);
  RAM ram_1 (
    .addr(address_register_q), .we(write_enable), .oe(not_1_out), .clk(clock_1_out), .din(input_register_q),
    .dout(ram_1_dout));
endmodule

module ALU_AC (
  input  C_in,
  input  [1:0] S,
  input  [7:0] A,
  input  [7:0] B,
  output [7:0] G,
  output C_out
);

  wire and_1_out, and_2_out, and_3_out, and_4_out, and_5_out, and_6_out, and_7_out, and_8_out, and_9_out,
       and_10_out, and_11_out, and_12_out, and_13_out, and_14_out, and_15_out, and_16_out, not_1_out,
       not_2_out, not_3_out, not_4_out, not_5_out, not_6_out, not_7_out, not_8_out;
  wire [7:0] or_1_out;

  not not_1 (not_1_out, B[0]);
  not not_2 (not_2_out, B[1]);
  not not_3 (not_3_out, B[2]);
  not not_4 (not_4_out, B[3]);
  not not_5 (not_5_out, B[4]);
  not not_6 (not_6_out, B[5]);
  not not_7 (not_7_out, B[6]);
  not not_8 (not_8_out, B[7]);
  and and_1 (and_1_out, B[0], S[0]);
  and and_2 (and_2_out, not_1_out, S[1]);
  and and_3 (and_3_out, B[1], S[0]);
  and and_4 (and_4_out, not_2_out, S[1]);
  and and_5 (and_5_out, B[2], S[0]);
  and and_6 (and_6_out, not_3_out, S[1]);
  and and_7 (and_7_out, B[3], S[0]);
  and and_8 (and_8_out, not_4_out, S[1]);
  and and_9 (and_9_out, B[4], S[0]);
  and and_10 (and_10_out, not_5_out, S[1]);
  and and_11 (and_11_out, B[5], S[0]);
  and and_12 (and_12_out, not_6_out, S[1]);
  and and_13 (and_13_out, B[6], S[0]);
  and and_14 (and_14_out, not_7_out, S[1]);
  and and_15 (and_15_out, B[7], S[0]);
  and and_16 (and_16_out, not_8_out, S[1]);
  or or_1 (or_1_out[0], and_1_out, and_2_out);
  or or_2 (or_1_out[1], and_3_out, and_4_out);
  or or_3 (or_1_out[2], and_5_out, and_6_out);
  or or_4 (or_1_out[3], and_7_out, and_8_out);
  or or_5 (or_1_out[4], and_9_out, and_10_out);
  or or_6 (or_1_out[5], and_11_out, and_12_out);
  or or_7 (or_1_out[6], and_13_out, and_14_out);
  or or_8 (or_1_out[7], and_15_out, and_16_out);
  Adder adder_1 (.a(A), .b(or_1_out), .out(G), .cin(C_in), .cout(C_out));
endmodule

module ALU_LC (
  input  [1:0] S,
  input  [7:0] A,
  input  [7:0] B,
  output [7:0] G
);

  wire [7:0] and_1_out, not_1_out, or_1_out, xor_1_out;

  assign and_1_out = A & B;  // AND_Gate and_1, 8 bits wide
  assign or_1_out = A | B;  // OR_Gate or_1, 8 bits wide
  assign xor_1_out = A ^ B;  // XOR_Gate xor_1, 8 bits wide
  assign not_1_out = ~A;  // NOT_Gate not_1, 8 bits wide
  Multiplexer #(.select(2), .width(8)) multiplexer_1 (
    .in0(and_1_out), .in1(or_1_out), .in2(xor_1_out), .in3(not_1_out), .out(G), .sel(S));
endmodule

module ALU (
  input  C_in,
  input  [2:0] S,
  input  [7:0] A,
  input  [7:0] B,
  output C_overflow,
  output [7:0] G
);

  wire [7:0] alu_ac_1_g, alu_lc_1_g;

  ALU_AC alu_ac_1 (.C_in(C_in), .S(S[1:0]), .A(A), .B(B), .G(alu_ac_1_g), .C_out(C_overflow));
  ALU_LC alu_lc_1 (.S(S[1:0]), .A(A), .B(B), .G(alu_lc_1_g));
  Multiplexer #(.width(8)) multiplexer_1 (.in0(alu_ac_1_g), .in1(alu_lc_1_g), .out(G), .sel(S[2]));
endmodule

module Basic_Shifter (
  input  [7:0] A,
  input  Input_Left,
  input  Input_Right,
  input  [1:0] S,
  output [7:0] G
);

  wire undriven, undriven_2, undriven_3, undriven_4, undriven_5, undriven_6, undriven_7, undriven_8;

  // NoConnect on undriven
  Multiplexer #(.select(2)) multiplexer_1 (
    .in0(A[7]), .in1(Input_Right), .in2(A[6]), .in3(undriven), .out(G[7]), .sel(S));
  // NoConnect on undriven_2
  Multiplexer #(.select(2)) multiplexer_2 (.in0(A[6]), .in1(A[7]), .in2(A[5]), .in3(undriven_2), .out(G[6]), .sel(S));
  // NoConnect on undriven_3
  Multiplexer #(.select(2)) multiplexer_3 (.in0(A[5]), .in1(A[6]), .in2(A[4]), .in3(undriven_3), .out(G[5]), .sel(S));
  // NoConnect on undriven_4
  Multiplexer #(.select(2)) multiplexer_4 (.in0(A[4]), .in1(A[5]), .in2(A[3]), .in3(undriven_4), .out(G[4]), .sel(S));
  // NoConnect on undriven_5
  Multiplexer #(.select(2)) multiplexer_5 (.in0(A[3]), .in1(A[4]), .in2(A[2]), .in3(undriven_5), .out(G[3]), .sel(S));
  // NoConnect on undriven_6
  Multiplexer #(.select(2)) multiplexer_6 (.in0(A[2]), .in1(A[3]), .in2(A[1]), .in3(undriven_6), .out(G[2]), .sel(S));
  // NoConnect on undriven_7
  Multiplexer #(.select(2)) multiplexer_7 (.in0(A[1]), .in1(A[2]), .in2(A[0]), .in3(undriven_7), .out(G[1]), .sel(S));
  // NoConnect on undriven_8
  Multiplexer #(.select(2)) multiplexer_8 (
    .in0(A[0]), .in1(A[1]), .in2(Input_Left), .in3(undriven_8), .out(G[0]), .sel(S));
endmodule

module ProgramCounter (
  input  reset,
  input  increment,
  output [7:0] Instruction_pointer
);

  wire multiplexer_2_out;
  wire [7:0] adder_1_out, multiplexer_1_out;

  Multiplexer #(.width(8)) multiplexer_1 (.in0(adder_1_out), .in1({8{1'b1}}), .out(multiplexer_1_out), .sel(reset));
  Register counter_register (
    .D(multiplexer_1_out), .en(multiplexer_2_out), .clk(multiplexer_2_out), .Q(Instruction_pointer));  // open: clr
  Multiplexer multiplexer_2 (.in0(increment), .in1(reset), .out(multiplexer_2_out), .sel(reset));
  Adder adder_1 (.a(8'h1), .b(Instruction_pointer), .out(adder_1_out));  // open: cin, cout
endmodule

module InstructionDecoder (
  input  next_instruction,
  input  [3:0] Instruction,
  input  [7:0] variable_A,
  input  [7:0] variable_B,
  input  [7:0] variable_C,
  output PC_next_instruction,
  output RF_enable_write,
  output [1:0] RF_address_write,
  output [1:0] RF_address_output_A,
  output [1:0] RF_address_output_B,
  output [3:0] FU_select_alu,
  output [1:0] FU_select_shifter,
  output FU_enable_output,
  output FU_output_alu_or_shifter,
  output RAM_enable_write,
  output RAM_enable_read,
  output [7:0] RAM_address
);

  wire decoder_1_out2, decoder_1_out3, decoder_1_out4, or_1_out;

  Decoder #(.select(4)) decoder_1 (
    .out2(decoder_1_out2), .out3(decoder_1_out3), .out4(decoder_1_out4), .sel(Instruction), .en(1'b1));  // open: out0, out1, out5, out6, out7, out8, out9, out10, out11, out12, out13, out14, out15
  assign RF_address_write = decoder_1_out2 ? variable_A[1:0] : 2'bz;  // Controlled_Buffer controlled_buffer_1
  assign RF_address_output_A = decoder_1_out2 ? variable_B[1:0] : 2'bz;  // Controlled_Buffer controlled_buffer_2
  assign RF_address_output_B = decoder_1_out2 ? variable_C[1:0] : 2'bz;  // Controlled_Buffer controlled_buffer_3
  assign RF_address_write = decoder_1_out4 ? variable_A[1:0] : 2'bz;  // Controlled_Buffer controlled_buffer_4
  assign RF_address_output_A = decoder_1_out3 ? variable_A[1:0] : 2'bz;  // Controlled_Buffer controlled_buffer_5
  assign RAM_address = decoder_1_out3 ? variable_B : 8'bz;  // Controlled_Buffer controlled_buffer_6
  assign RAM_address = decoder_1_out4 ? variable_B : 8'bz;  // Controlled_Buffer controlled_buffer_7
  or or_1 (or_1_out, decoder_1_out4, decoder_1_out2);
  or or_2 (RF_enable_write, 1'b0, or_1_out);
  buf or_3 (FU_select_alu[0], 1'b0);  // OR_Gate
  or or_4 (FU_select_alu[1], 1'b0, decoder_1_out2);
  buf or_5 (FU_select_alu[2], 1'b0);  // OR_Gate
  buf or_6 (FU_select_alu[3], 1'b0);  // OR_Gate
  buf or_7 (FU_select_shifter[0], 1'b0);  // OR_Gate
  buf or_8 (FU_select_shifter[1], 1'b0);  // OR_Gate
  or or_9 (FU_enable_output, 1'b0, decoder_1_out2);
  buf or_10 (FU_output_alu_or_shifter, 1'b0);  // OR_Gate
  or or_11 (RAM_enable_write, 1'b0, decoder_1_out3);
  or or_12 (RAM_enable_read, 1'b0, decoder_1_out4);

  assign PC_next_instruction = next_instruction;

  // Notes on the sheet:
  //   register_A
  //   A
  //   register_A
  //   register_B
  //   B
  //   C
  //   register_C
  //   0010
  //   0011
  //   0100
endmodule

module FunctionUnit (
  input  [7:0] Input_A,
  input  [7:0] Input_B,
  input  [3:0] select_alu,
  input  [1:0] select_shifter,
  input  select_alu_or_shifter,
  input  enable_ouput,
  output overflow,
  output [7:0] Output_FU
);

  wire [7:0] alu_1_g, basic_shifter_1_g, multiplexer_1_out;

  ALU alu_1 (.C_in(select_alu[0]), .S(select_alu[3:1]), .A(Input_A), .B(Input_B), .C_overflow(overflow), .G(alu_1_g));
  Basic_Shifter basic_shifter_1 (
    .A(Input_B), .Input_Left(1'b0), .Input_Right(1'b0), .S(select_shifter), .G(basic_shifter_1_g));
  Multiplexer #(.width(8)) multiplexer_1 (
    .in0(alu_1_g), .in1(basic_shifter_1_g), .out(multiplexer_1_out), .sel(select_alu_or_shifter));
  assign Output_FU = enable_ouput ? multiplexer_1_out : 8'bz;  // Controlled_Buffer controlled_buffer_1
endmodule

module RegisterFile (
  input  [7:0] Input_RF,
  input  enable_write,
  input  [1:0] address_write,
  input  [1:0] address_output_A,
  input  [1:0] address_output_B,
  input  clock,
  output [7:0] Output_A,
  output [7:0] Output_B
);

  wire and_1_out, decoder_1_out0, decoder_1_out1, decoder_1_out2, decoder_1_out3;
  wire [7:0] registre_0_q, registre_1_q, registre_2_q, registre_3_q;

  and and_1 (and_1_out, enable_write, clock);
  Decoder #(.select(2)) decoder_1 (
    .out0(decoder_1_out0), .out1(decoder_1_out1), .out2(decoder_1_out2), .out3(decoder_1_out3),
    .sel(address_write), .en(and_1_out));
  Register #(.trigger("high")) registre_0 (
    .D(Input_RF), .en(decoder_1_out0), .clk(decoder_1_out0), .Q(registre_0_q));  // open: clr
  Register #(.trigger("high")) registre_1 (
    .D(Input_RF), .en(decoder_1_out1), .clk(decoder_1_out1), .Q(registre_1_q));  // open: clr
  Register #(.trigger("high")) registre_2 (
    .D(Input_RF), .en(decoder_1_out2), .clk(decoder_1_out2), .Q(registre_2_q));  // open: clr
  Register #(.trigger("high")) registre_3 (
    .D(Input_RF), .en(decoder_1_out3), .clk(decoder_1_out3), .Q(registre_3_q));  // open: clr
  Multiplexer #(.select(2), .width(8)) multiplexer_1 (
    .in0(registre_0_q), .in1(registre_1_q), .in2(registre_2_q), .in3(registre_3_q), .out(Output_A),
    .sel(address_output_A));
  Multiplexer #(.select(2), .width(8)) multiplexer_2 (
    .in0(registre_0_q), .in1(registre_1_q), .in2(registre_2_q), .in3(registre_3_q), .out(Output_B),
    .sel(address_output_B));
endmodule

module frequencyDiviser (
  input  clock,
  output clock_instruction,
  output clock_dirac,
  output [7:0] out_4
);

  wire d_ff_1_q, d_ff_1_qn, d_ff_2_q, d_ff_2_qn, not_1_out;

  LED led_1 (.in(clock));
  not not_1 (not_1_out, clock);
  D_Flip_Flop d_ff_1 (.D(d_ff_1_qn), .clk(clock), .Q(d_ff_1_q), .Qn(d_ff_1_qn));  // open: preset, reset
  LED led_2 (.in(d_ff_1_q));
  D_Flip_Flop d_ff_2 (.D(d_ff_2_qn), .clk(d_ff_1_q), .Q(d_ff_2_q), .Qn(d_ff_2_qn));  // open: preset, reset
  LED led_3 (.in(d_ff_2_q));
  and and_1 (clock_instruction, clock, d_ff_1_q, d_ff_2_q);
  and and_2 (clock_dirac, d_ff_2_q, d_ff_1_q, not_1_out);
  ProgramCounter programcounter_1 (.increment(clock_instruction), .Instruction_pointer(out_4));  // open: reset
endmodule
